# Fritzing sketch schematics (saved by Fritzing 0.9.3b)
circuit board: 6.46869cm x 8.86073cm
breadboards: 1

parts:
  NODEMCU1_0 = NodeMCU V1.0
  BLUETOOTH = Header 6 [package=molex-1x6-ra]
  DHT22 = Header 3 [package=molex-1x3_lock]
  PMS3003 = Header 4 [package=molex-1x4_lock]
  I2C-M = Header 4 [package=molex-1x4_lock]
  BC547 = PNP-Transistor [package="TO92 [THT]"]
  BT-BUTTON = Camdenboss CTB0158-2 [part_number=CTB0158-2 package=THT]
  J1 = Camdenboss CTB0158-2 [part_number=CTB0158-2 package=THT]
  part = TP4056 [chip_label=TP4056 package="DIP (Dual Inline) [THT]"]
  J2 = Camdenboss CTB0158-2 [part_number=CTB0158-2 package=THT]
  J3 = Camdenboss CTB0158-2 [part_number=CTB0158-2 package=THT]
  J4 = Camdenboss CTB0158-2 [part_number=CTB0158-2 package=THT]
  J5 = Camdenboss CTB0158-2 [part_number=CTB0158-2 package=THT]
  J6 = Camdenboss CTB0158-2 [part_number=CTB0158-2 package=THT]
  J7 = Camdenboss CTB0158-2 [part_number=CTB0158-2 package=THT]
  R1 = Resistor [tolerance=±5% resistance=10k package=THT]

nets:
  N1: NODEMCU1_0.D0, BLUETOOTH.2
  N2: NODEMCU1_0.D1, I2C-M.1
  N3: NODEMCU1_0.D2, I2C-M.2
  N4: NODEMCU1_0.D3, PMS3003.3
  N5: NODEMCU1_0.D4, BLUETOOTH.3
  N6: NODEMCU1_0.GND, DHT22.3, PMS3003.1, I2C-M.4, BC547.C, J5.pin1, R1.Pin_0
  N7: NODEMCU1_0.D5, PMS3003.4
  N8: NODEMCU1_0.D6, DHT22.2
  N9: NODEMCU1_0.D7, BT-BUTTON.pin2, R1.Pin_1
  N10: NODEMCU1_0.D8, BC547.B
  N11: NODEMCU1_0.Vin, BLUETOOTH.5, DHT22.1, PMS3003.2, I2C-M.3, BT-BUTTON.pin1, J3.pin2
  N12: BLUETOOTH.4, BC547.E
  N13: J1.pin1, part.pin1
  N14: J1.pin2, part.pin2
  N15: part.pin3, J7.pin1
  N16: part.pin4, J2.pin2
  N17: part.pin5, J2.pin1
  N18: part.pin6, J6.pin2
  N19: J3.pin1, J4.pin1

notes:
  GND
  VCC
  Rx
  Tx
  D
  SCL
  SDA
  STATE
  EN_M
  [JUMP]
  Solder
  B-
  B+
  10 K
  Power Button
  BT- Button

custom parts:
  NodeMCU V1.0: ESP8266 based NodeMCU
  TP4056: A DIP stand-in part for whatever IC you want. With 6 pins on a 300mil dual inline package (DIP) footprint.
